# Fritzing sketch Calculator (saved by Fritzing 0.8.7b)
breadboards: 1

parts:
  U1 = LCD-16X2 [package=lcd-16x2]
  Componente1 = Arduino Micro (Rev3)  # not connected
  Matrix_keypad1 = KEYPAD 4x4  # not connected
  S1 = Pushbutton [package="[THT]"]
  S2 = Pushbutton [package="[THT]"]
  R1 = TRIMPOT [package=trimpot_pth_s3_lock]

nets:
  N1: U1.VSS, U1.R_W, R1.CW
  N2: U1.VDD, R1.CCW
  N3: U1.VO, R1.WIPER
  N4: S1.Pin_1, S1.Pin_2
  N5: S1.Pin_3, S1.Pin_4
  N6: S2.Pin_1, S2.Pin_2
  N7: S2.Pin_3, S2.Pin_4

custom parts:
  KEYPAD 4x4: Matrix keypad 16 buttons, 4 rows x 4 columns
